// Logisim project Fool Adder.circ as structural Verilog: 1 circuit, main circuit main
module main (
  input  in_1,
  input  in_2,
  input  in_3,
  input  in_4,
  output out,
  output Carry,
  output out_2,
  output Carry_2
);

  wire and_1_out, and_2_out, not_1_out, not_2_out, or_1_out, or_2_out;

  and and_1 (and_1_out, in_1, in_2);
  or or_1 (or_1_out, in_1, in_2);
  and and_2 (and_2_out, in_3, in_4);
  or or_2 (or_2_out, in_3, in_4);
  not not_1 (not_1_out, and_1_out);
  not not_2 (not_2_out, and_2_out);
  and and_3 (out, not_1_out, or_1_out);
  and and_4 (Carry, in_1, in_2);
  and and_5 (out_2, not_2_out, or_2_out);
  and and_6 (Carry_2, in_3, in_4);

  // Notes on the sheet:
  //   Half Adder
  //   XOR GATE
  //   XOR GATE
endmodule
